# Fritzing sketch Zujalica v3 (saved by Fritzing 0.9.3b)
circuit board: 5cm x 1.3cm
breadboards: 1

parts:
  U1 = SN74LS20N [package="DIP14 [THT]"]
  U2 = LIPO-110mAh [package=lipo-110]
  J1 = female pin header, 2 pins [form="♀ (female)"]
  LED1 = LED - 5mm [color="Blue (430nm)" package="5 mm [THT]"]
  R2 = Resistor [tolerance=±5% resistance=470 package=THT]
  R3 = Resistor [tolerance=±5% resistance=220k package=THT]
  C1 = Electrolytic Capacitor [capacitance=1µF package="100 mil [THT, electrolytic]"]
  R1 = Resistor [tolerance=±5% resistance=100k package=THT]
  J3 = female pin header, 1 pin [form="♀ (female)"]
  J4 = female pin header, 1 pin [form="♀ (female)"]
  SG1 = Buzzer 12mm [package=buzzer-12mm-ns]

nets:
  N1: U1.1A, J1.pin1, R1.Pin_0
  N2: U1.1B, U1.1C, LED1.anode
  N3: U1.NC#2, C1.+
  N4: U1.1D, U1.1Y, U1.2Y, U1.2A, R3.Pin_1, C1.-
  N5: U1.GND, U2.-, J1.pin2, R3.Pin_0, J4.pin1
  N6: U1.2B, SG1.2
  N7: U1.VCC, U2.+, R2.Pin_1, R1.Pin_1, J3.pin1, SG1.1
  N8: LED1.cathode, R2.Pin_0
